// Logisim project BigASM Bubble Sort.circ as structural Verilog
module BOARD_BIG_ASM (
  output out_1
);

  wire button_1_out, CLK, CLR, d_ff_1_q, not_1_out, Write, Write_ASCII;
  wire [6:0] ASCII;
  wire [7:0] counter_1_q;
  wire [23:0] Dir_INPUT, Dir_MEMORY;
  wire [31:0] INPUT, MEMORY_IN, MEMORY_OUT;

  Button button_1 (.out(button_1_out));
  Clock clock_1 (.out(CLK));
  D_Flip_Flop d_ff_1 (.clk(CLK), .D(1'b1), .Q(d_ff_1_q), .reset(button_1_out));  // open: Qn, preset, en
  D_Flip_Flop d_ff_2 (.clk(CLK), .D(d_ff_1_q), .Qn(CLR), .reset(button_1_out));  // open: Q, preset, en
  BIG_ASM big_asm_1 (
    .DATA_INPUT(INPUT), .MEMORY_IN(MEMORY_OUT), .CLK(CLK), .CLR(CLR), .DIR_INPUT(Dir_INPUT),
    .MEMORY_OUT(MEMORY_IN), .DIR_MEMORY(Dir_MEMORY), .Write_OUTPUT(Write), .ASCII(ASCII),
    .Write_ASCII(Write_ASCII), .END(out_1));
  MEMORY memory_1 (.DIR(Dir_MEMORY), .DATA_IN(MEMORY_IN), .WRITE(Write), .CLK(CLK), .CLR(CLR), .DATA_OUT(MEMORY_OUT));
  INPUT input_1 (.DIR(Dir_INPUT), .CLK(CLK), .DATA_OUT(INPUT));
  Counter counter_1 (.load(1'b0), .count(not_1_out), .Q(counter_1_q), .clk(CLK), .clr(CLR));  // open: D, carry
  not not_1 (not_1_out, out_1);
  // Probe on counter_1_q
  TTY #(.rows(32), .cols(60)) tty_1 (.data(ASCII), .clk(CLK), .we(Write_ASCII), .clr(CLR));

  // Other names for the same wires on the sheet: END = out_1

  // Notes on the sheet:
  //   COUNTER
  //   BOARD
endmodule

module INPUT (
  input  [23:0] DIR,
  input  CLK,
  output [31:0] DATA_OUT
);

  RAM #(.addrWidth(24), .dataWidth(32)) ram_1 (.addr(DIR), .data(DATA_OUT), .clk(CLK), .ld(1'b1));  // open: sel, clr
endmodule

module MEMORY (
  input  [23:0] DIR,
  input  [31:0] DATA_IN,
  input  WRITE,
  input  CLK,
  input  CLR,
  output [31:0] DATA_OUT
);

  RAM #(.addrWidth(24), .dataWidth(32), .bus("separate")) ram_1 (
    .addr(DIR), .din(DATA_IN), .data(DATA_OUT), .str(WRITE), .clk(CLK), .clr(CLR));  // open: sel, ld
endmodule

module BIG_ASM (
  input  [31:0] DATA_INPUT,
  input  [31:0] MEMORY_IN,
  input  CLK,
  input  CLR,
  output [23:0] DIR_INPUT,
  output [31:0] MEMORY_OUT,
  output [6:0] ASCII,
  output Write_ASCII,
  output [23:0] DIR_MEMORY,
  output END,
  output Write_OUTPUT
);

  Bubble_Sort bubble_sort_1 (
    .CLK(CLK), .Start(CLR), .Data_Input(DATA_INPUT), .Memory_Input(MEMORY_IN), .Write(Write_OUTPUT),
    .Memory_Out(MEMORY_OUT), .Dir_Memory(DIR_INPUT), .ASCII(ASCII), .W_ASCII(Write_ASCII), .END(END));

  assign DIR_MEMORY = DIR_INPUT;

  // Other names for the same wires on the sheet: DI[31:0] = DATA_INPUT; DM[23:0] = DIR_INPUT; MI[31:0] = MEMORY_IN;
  //   MO[31:0] = MEMORY_OUT; Write = Write_OUTPUT
endmodule

module PRINT_UDEC (
  input  [31:0] num,
  input  start,
  input  CLK,
  input  RST,
  output [6:0] ASCII,
  output Write_ASCII,
  output \end 
);

  wire _0_c, _0_n, demultiplexer_1_out0, demultiplexer_2_out0, demultiplexer_2_out1, demultiplexer_3_out0,
       demultiplexer_3_out1, IDLE_2_q, IDLE_3_q, IDLE_4_q, IDLE_q, Lc, Lc_0, Ln, Ln_0, or_1_out;
  wire [23:0] bit_extender_1_out;
  wire [31:0] c, c___1, c___1_t, divider_1_rem, memory_1_data_out, multiplexer_1_out, multiplexer_2_out,
       multiplexer_3_out, n, n___10, n___10___48;

  Multiplexer #(.width(32), .enable("false")) multiplexer_1 (
    .in0(num), .in1(n___10), .out(multiplexer_1_out), .sel(Lc_0));
  Divider #(.width(32)) divider_1 (.a(n), .b(32'ha), .out(n___10), .rem(divider_1_rem));  // open: upper
  Adder #(.width(32)) adder_1 (.a(divider_1_rem), .b(32'h30), .out(n___10___48));  // open: cin, cout
  or or_1 (or_1_out, demultiplexer_1_out0, \end );
  Register #(.width(32)) u_n (.D(multiplexer_1_out), .en(Ln), .Q(n), .clk(CLK), .clr(RST));
  D_Flip_Flop IDLE (.clk(CLK), .D(or_1_out), .Q(IDLE_q), .preset(RST));  // open: Qn, en, reset
  Demultiplexer #(.enable("false")) demultiplexer_1 (
    .out0(demultiplexer_1_out0), .out1(Ln_0), .in(IDLE_q), .sel(start));
  or or_2 (Write_ASCII, demultiplexer_3_out0, demultiplexer_2_out1);
  Multiplexer #(.width(32), .enable("false")) multiplexer_2 (
    .in0(c___1), .in1(c___1_t), .out(multiplexer_2_out), .sel(Write_ASCII));
  Adder #(.width(32)) adder_2 (.a(c), .b(32'h1), .out(c___1));  // open: cin, cout
  Subtractor #(.width(32)) subtractor_1 (.a(c), .b(32'h1), .out(c___1_t));  // open: bin, bout
  D_Flip_Flop IDLE_2 (.clk(CLK), .D(Ln_0), .Q(IDLE_2_q), .reset(RST));  // open: Qn, preset, en
  Register #(.width(32)) u_c (.D(multiplexer_2_out), .en(Lc), .Q(c), .clk(CLK), .clr(RST));
  or or_3 (Lc_0, IDLE_2_q, demultiplexer_3_out1);
  Multiplexer #(.width(32), .enable("false")) multiplexer_3 (
    .in0(c), .in1(c___1_t), .out(multiplexer_3_out), .sel(Write_ASCII));
  Comparator #(.width(32), .mode("unsigned")) comparator_1 (.a({32{1'b0}}), .b(n), .lt(_0_n));  // open: gt, eq
  Comparator #(.width(32), .mode("unsigned")) comparator_2 (.a({32{1'b0}}), .b(c), .lt(_0_c));  // open: gt, eq
  D_Flip_Flop IDLE_3 (.clk(CLK), .D(Write_ASCII), .Q(IDLE_3_q), .reset(RST));  // open: Qn, preset, en
  Demultiplexer #(.enable("false")) demultiplexer_2 (
    .out0(demultiplexer_2_out0), .out1(demultiplexer_2_out1), .in(IDLE_3_q), .sel(_0_c));
  Bit_Extender #(.in_width(32), .out_width(24)) bit_extender_1 (.in(multiplexer_3_out), .out(bit_extender_1_out));
  D_Flip_Flop IDLE_4 (.clk(CLK), .D(Lc_0), .Q(IDLE_4_q), .reset(RST));  // open: Qn, preset, en
  or or_4 (Lc, Lc_0, Write_ASCII);
  or or_5 (Ln, Ln_0, Lc_0);
  Demultiplexer #(.enable("false")) demultiplexer_3 (
    .out0(demultiplexer_3_out0), .out1(demultiplexer_3_out1), .in(IDLE_4_q), .sel(_0_n));
  D_Flip_Flop IDLE_5 (.clk(CLK), .D(demultiplexer_2_out0), .Q(\end ), .reset(RST));  // open: Qn, preset, en
  MEMORY memory_1 (
    .DIR(bit_extender_1_out), .DATA_IN(n___10___48), .WRITE(Lc_0), .CLK(CLK), .CLR(RST),
    .DATA_OUT(memory_1_data_out));
  Bit_Extender #(.in_width(32), .out_width(7)) bit_extender_2 (.in(memory_1_data_out), .out(ASCII));

  // Other names for the same wires on the sheet: Lc_1 = Write_ASCII; Sc = Write_ASCII; Ln_1 = Lc_0; Sn = Lc_0;
  //   Write = Lc_0
endmodule

module PRINT_DEC (
  input  [31:0] num,
  input  start,
  input  CLK,
  input  RST,
  output [6:0] ASCII,
  output Write_ASCII,
  output END
);

  wire demultiplexer_1_out0, demultiplexer_1_out1, demultiplexer_2_out0, demultiplexer_3_out0, end_t,
       IDLE_3_q, IDLE_q, or_1_out, or_2_out, or_3_out, S_ASCII, startUDEC, Write_ASCII_1;
  wire [6:0] ASCII_t;
  wire [31:0] multiplexer_1_out, negator_1_out;

  or or_1 (or_1_out, demultiplexer_1_out0, END);
  Negator #(.width(32)) negator_1 (.in(num), .out(negator_1_out));
  D_Flip_Flop IDLE (.clk(CLK), .D(or_1_out), .Q(IDLE_q), .preset(RST));  // open: Qn, en, reset
  Demultiplexer #(.enable("false")) demultiplexer_1 (
    .out0(demultiplexer_1_out0), .out1(demultiplexer_1_out1), .in(IDLE_q), .sel(start));
  Multiplexer #(.width(32), .enable("false")) multiplexer_1 (
    .in0(num), .in1(negator_1_out), .out(multiplexer_1_out), .sel(num[31]));
  Demultiplexer #(.enable("false")) demultiplexer_2 (
    .out0(demultiplexer_2_out0), .out1(S_ASCII), .in(demultiplexer_1_out1), .sel(num[31]));
  or or_2 (or_2_out, demultiplexer_2_out0, S_ASCII);
  D_Flip_Flop IDLE_2 (.clk(CLK), .D(or_2_out), .Q(startUDEC), .reset(RST));  // open: Qn, preset, en
  PRINT_UDEC print_udec_1 (
    .num(multiplexer_1_out), .start(startUDEC), .CLK(CLK), .RST(RST), .ASCII(ASCII_t),
    .Write_ASCII(Write_ASCII_1), .\end (end_t));
  D_Flip_Flop IDLE_3 (.clk(CLK), .D(or_3_out), .Q(IDLE_3_q), .reset(RST));  // open: Qn, preset, en
  or or_3 (or_3_out, startUDEC, demultiplexer_3_out0);
  Demultiplexer #(.enable("false")) demultiplexer_3 (
    .out0(demultiplexer_3_out0), .out1(END), .in(IDLE_3_q), .sel(end_t));
  Multiplexer #(.width(7), .enable("false")) multiplexer_2 (
    .in0(ASCII_t), .in1(7'b0101101), .out(ASCII), .sel(S_ASCII));
  or or_4 (Write_ASCII, S_ASCII, Write_ASCII_1);

  // Other names for the same wires on the sheet: sign = num[31]; Write_ASCII_0 = S_ASCII
endmodule

module TEST_PRINT (
  input  [31:0] in_1,
  output out_2
);

  wire button_1_out, button_2_out, CLK, CLR, d_ff_1_q, Write_ASCII;
  wire [6:0] ASCII;

  Button button_1 (.out(button_1_out));
  Clock clock_1 (.out(CLK));
  D_Flip_Flop d_ff_1 (.clk(CLK), .D(1'b1), .Q(d_ff_1_q), .reset(button_1_out));  // open: Qn, preset, en
  D_Flip_Flop d_ff_2 (.clk(CLK), .D(d_ff_1_q), .Qn(CLR), .reset(button_1_out));  // open: Q, preset, en
  Button button_2 (.out(button_2_out));
  PRINT_UDEC print_udec_1 ();  // open: num, start, CLK, RST, ASCII, Write_ASCII, end
  PRINT_DEC print_dec_1 (
    .num(in_1), .start(button_2_out), .CLK(CLK), .RST(CLR), .ASCII(ASCII), .Write_ASCII(Write_ASCII),
    .END(out_2));
  TTY #(.rows(32), .cols(60)) tty_1 (.data(ASCII), .clk(CLK), .we(Write_ASCII), .clr(CLR));
endmodule

module Data_Path (
  input  [1:0] S_Dir_Memory,
  input  [1:0] S_Memory_Out,
  input  CLK,
  input  L_j,
  input  S_j,
  input  L_i,
  input  S_i,
  input  RST_i,
  input  L_A___j,
  input  L_A___j___1,
  input  L_len,
  input  [31:0] Data_Input,
  input  [31:0] Memory_Input,
  output j___len___i___1,
  output [23:0] Dir_Memory,
  output A___j_____A___j___1,
  output i___len,
  output i____len,
  output [31:0] Lenght,
  output [31:0] Memory_Out
);

  wire comparator_3_eq;
  wire [23:0] i, i_plus_plus, j, j_plus_plus, multiplexer_1_out, multiplexer_2_out;
  wire [31:0] A___j, A___j___1, bit_extender_1_out, bit_extender_2_out, bit_extender_3_out, len___i___1,
       subtractor_1_out;

  Multiplexer #(.width(24), .enable("false")) multiplexer_1 (
    .in0(24'h1), .in1(i_plus_plus), .out(multiplexer_1_out), .sel(S_i));
  Register #(.width(24)) u_i (.D(multiplexer_1_out), .en(L_i), .Q(i), .clk(CLK), .clr(RST_i));
  Multiplexer #(.width(24), .enable("false")) multiplexer_2 (
    .in0(24'h1), .in1(j_plus_plus), .out(multiplexer_2_out), .sel(S_j));
  assign bit_extender_1_out = {{8{1'b0}}, j};  // Bit_Extender bit_extender_1
  Comparator #(.width(32)) comparator_1 (
    .a(bit_extender_1_out), .b(len___i___1), .lt(j___len___i___1));  // open: gt, eq
  Comparator #(.width(32)) comparator_2 (.a(A___j), .b(A___j___1), .lt(A___j_____A___j___1));  // open: gt, eq
  Adder #(.width(24)) adder_1 (.a(i), .b(24'h1), .out(i_plus_plus));  // open: cin, cout
  Register #(.width(24)) u_j (.D(multiplexer_2_out), .en(L_j), .Q(j), .clk(CLK));  // open: clr
  Register #(.width(32)) u_A___j (.D(Memory_Input), .en(L_A___j), .Q(A___j), .clk(CLK));  // open: clr
  assign bit_extender_2_out = {{8{1'b0}}, i};  // Bit_Extender bit_extender_2
  Adder #(.width(24)) adder_2 (.a(j), .b(24'h1), .out(j_plus_plus));  // open: cin, cout
  Subtractor #(.width(32)) subtractor_1 (
    .a(Lenght), .b(bit_extender_2_out), .out(subtractor_1_out));  // open: bin, bout
  assign bit_extender_3_out = {{8{1'b0}}, i};  // Bit_Extender bit_extender_3
  Register #(.width(32)) u_A___j___1 (.D(Memory_Input), .en(L_A___j___1), .Q(A___j___1), .clk(CLK));  // open: clr
  Adder #(.width(32)) adder_3 (.a(subtractor_1_out), .b(32'h1), .out(len___i___1));  // open: cin, cout
  or or_1 (i____len, comparator_3_eq, i___len);
  Comparator #(.width(32)) comparator_3 (
    .a(bit_extender_3_out), .b(Lenght), .eq(comparator_3_eq), .lt(i___len));  // open: gt
  Register #(.width(32)) u_Lenght (.D(Data_Input), .en(L_len), .Q(Lenght), .clk(CLK));  // open: clr
  Multiplexer #(.select(2), .width(24), .enable("false")) multiplexer_3 (
    .in0(i), .in1(j), .in2(j_plus_plus), .out(Dir_Memory), .sel(S_Dir_Memory));  // open: in3
  Multiplexer #(.select(2), .width(32), .enable("false")) multiplexer_4 (
    .in0(Data_Input), .in1(A___j), .in2(A___j___1), .out(Memory_Out), .sel(S_Memory_Out));  // open: in3

  // Other names for the same wires on the sheet: DI[31:0] = Data_Input; len[31:0] = Lenght; MI[31:0] = Memory_Input;
  //   S_DM[1:0] = S_Dir_Memory; S_MO[1:0] = S_Memory_Out
endmodule

module Copy (
  input  CLK,
  input  Start,
  input  i____len,
  output End,
  output L_i,
  output S_i,
  output Write,
  output L_len,
  output RST_i
);

  wire d_ff_1_q, d_ff_2_q, demultiplexer_1_out0, demultiplexer_3_out0, demultiplexer_3_out1, IDLE_q,
       or_1_out, or_2_out, or_4_out;

  D_Flip_Flop IDLE (.clk(CLK), .D(or_1_out), .Q(IDLE_q), .preset(Start));  // open: Qn, en, reset
  or or_1 (or_1_out, demultiplexer_1_out0, demultiplexer_3_out1);
  Demultiplexer #(.enable("false")) demultiplexer_1 (
    .out0(demultiplexer_1_out0), .out1(L_len), .in(IDLE_q), .sel(Start));
  or or_2 (or_2_out, L_len, S_i);
  D_Flip_Flop d_ff_1 (.clk(CLK), .D(or_2_out), .Q(d_ff_1_q));  // open: Qn, preset, en, reset
  Demultiplexer #(.enable("false")) demultiplexer_2 (.out0(End), .out1(S_i), .in(d_ff_1_q), .sel(i____len));
  or or_3 (L_i, S_i, L_len);
  or or_4 (or_4_out, demultiplexer_3_out0, End);
  D_Flip_Flop d_ff_2 (.clk(CLK), .D(or_4_out), .Q(d_ff_2_q));  // open: Qn, preset, en, reset
  Demultiplexer #(.enable("false")) demultiplexer_3 (
    .out0(demultiplexer_3_out0), .out1(demultiplexer_3_out1), .in(d_ff_2_q), .sel(Start));

  assign RST_i = Start;
  assign Write = S_i;

  // Other names for the same wires on the sheet: L_i0 = L_len; L_i1 = S_i
endmodule

module Control_Unit (
  input  CLK,
  input  Start,
  input  i___len,
  input  j___len___i___1,
  input  A___j_____A___j___1,
  output End,
  output L_i,
  output S_i,
  output L_j,
  output S_j,
  output Write,
  output L_A__j,
  output L_A__j___1,
  output [1:0] out_14,
  output [1:0] out_15
);

  wire d_ff_1_q, d_ff_2_q, d_ff_3_q, d_ff_4_q, d_ff_6_q, d_ff_7_q, d_ff_8_q, d_ff_9_q, d_ff_11_q, d_ff_12_q,
       d_ff_13_q, demultiplexer_1_out0, demultiplexer_3_out0, demultiplexer_3_out1, demultiplexer_4_out0,
       demultiplexer_5_out0, L_i0, L_j0, or_1_out, or_2_out, or_3_out, or_4_out;

  or or_1 (or_1_out, demultiplexer_1_out0, demultiplexer_3_out1);
  D_Flip_Flop d_ff_1 (.clk(CLK), .D(or_1_out), .Q(d_ff_1_q), .preset(Start));  // open: Qn, en, reset
  Demultiplexer #(.enable("false")) demultiplexer_1 (
    .out0(demultiplexer_1_out0), .out1(L_i0), .in(d_ff_1_q), .sel(Start));
  or or_2 (or_2_out, L_i0, d_ff_4_q);
  D_Flip_Flop d_ff_2 (.clk(CLK), .D(or_2_out), .Q(d_ff_2_q));  // open: Qn, preset, en, reset
  Demultiplexer #(.enable("false")) demultiplexer_2 (.out0(End), .out1(L_j0), .in(d_ff_2_q), .sel(i___len));
  D_Flip_Flop d_ff_3 (.clk(CLK), .D(or_3_out), .Q(d_ff_3_q));  // open: Qn, preset, en, reset
  or or_3 (or_3_out, demultiplexer_3_out0, End);
  D_Flip_Flop d_ff_4 (.clk(CLK), .D(S_i), .Q(d_ff_4_q));  // open: Qn, preset, en, reset
  Demultiplexer #(.enable("false")) demultiplexer_3 (
    .out0(demultiplexer_3_out0), .out1(demultiplexer_3_out1), .in(d_ff_3_q), .sel(Start));
  D_Flip_Flop d_ff_5 (.clk(CLK), .D(demultiplexer_4_out0), .Q(S_i));  // open: Qn, preset, en, reset
  D_Flip_Flop d_ff_6 (.clk(CLK), .D(or_4_out), .Q(d_ff_6_q));  // open: Qn, preset, en, reset
  or or_4 (or_4_out, L_j0, d_ff_7_q);
  Demultiplexer #(.enable("false")) demultiplexer_4 (
    .out0(demultiplexer_4_out0), .out1(L_A__j), .in(d_ff_6_q), .sel(j___len___i___1));
  or or_5 (Write, out_15[1], out_15[0]);
  or or_6 (out_14[0], L_A__j, out_15[1]);
  or or_7 (out_14[1], L_A__j___1, out_15[0]);
  D_Flip_Flop d_ff_7 (.clk(CLK), .D(d_ff_9_q), .Q(d_ff_7_q));  // open: Qn, preset, en, reset
  D_Flip_Flop d_ff_8 (.clk(CLK), .D(L_A__j), .Q(d_ff_8_q));  // open: Qn, preset, en, reset
  D_Flip_Flop d_ff_9 (.clk(CLK), .D(S_j), .Q(d_ff_9_q));  // open: Qn, preset, en, reset
  D_Flip_Flop d_ff_10 (.clk(CLK), .D(d_ff_8_q), .Q(L_A__j___1));  // open: Qn, preset, en, reset
  D_Flip_Flop d_ff_11 (.clk(CLK), .D(L_A__j___1), .Q(d_ff_11_q));  // open: Qn, preset, en, reset
  or or_8 (S_j, out_15[0], demultiplexer_5_out0);
  D_Flip_Flop d_ff_12 (.clk(CLK), .D(d_ff_11_q), .Q(d_ff_12_q));  // open: Qn, preset, en, reset
  Demultiplexer #(.enable("false")) demultiplexer_5 (
    .out0(demultiplexer_5_out0), .out1(out_15[1]), .in(d_ff_12_q), .sel(A___j_____A___j___1));
  D_Flip_Flop d_ff_13 (.clk(CLK), .D(out_15[1]), .Q(d_ff_13_q));  // open: Qn, preset, en, reset
  D_Flip_Flop d_ff_14 (.clk(CLK), .D(d_ff_13_q), .Q(out_15[0]));  // open: Qn, preset, en, reset
  or or_9 (L_i, L_i0, S_i);
  or or_10 (L_j, L_j0, S_j);

  // Other names for the same wires on the sheet: L_i1 = S_i; L_j1 = S_j; S_DM[1:0] = out_14; S_DM0 = out_14[0];
  //   S_DM1 = out_14[1]; S_DM00 = L_A__j; L_A___j___1 = L_A__j___1; S_DM10 = L_A__j___1; S_DM11 = out_15[0];
  //   S_MO[1:0] = out_15; S_MO0 = out_15[0]; Write1 = out_15[0]; S_DM01 = out_15[1]; S_MO1 = out_15[1];
  //   Write0 = out_15[1]
endmodule

module Bubble_Sort (
  input  CLK,
  input  Start,
  input  [31:0] Data_Input,
  input  [31:0] Memory_Input,
  output Write,
  output [31:0] Memory_Out,
  output [23:0] Dir_Memory,
  output END,
  output [6:0] ASCII,
  output W_ASCII
);

  wire A__j_____A__j___1, copy_1_end, d_ff_1_q, d_ff_2_q, d_ff_3_q, d_ff_5_q, d_ff_6_q, d_ff_7_q,
       demultiplexer_1_out0, demultiplexer_1_out1, demultiplexer_2_out0, demultiplexer_3_out0,
       demultiplexer_3_out1, demultiplexer_4_out0, End_CU, i____len, i___len, IDLE_q, j___len___i___1,
       L_A__j, L_A__j___1, L_i, L_i0, L_i1, L_i2, L_i3, L_j, L_len, or_1_out, or_2_out, or_3_out, ReStart,
       RST_i, S_i, S_i0, S_i1, S_j, Write0, Write1;
  wire [1:0] S_DM, S_MO;
  wire [31:0] len;

  or or_1 (or_1_out, demultiplexer_1_out0, ReStart);
  D_Flip_Flop d_ff_1 (.clk(CLK), .D(or_1_out), .Q(d_ff_1_q), .preset(Start));  // open: Qn, en, reset
  Demultiplexer #(.enable("false")) demultiplexer_1 (
    .out0(demultiplexer_1_out0), .out1(demultiplexer_1_out1), .in(d_ff_1_q), .sel(Start));
  D_Flip_Flop IDLE (.clk(CLK), .D(demultiplexer_2_out0), .Q(IDLE_q), .preset(End_CU));  // open: Qn, en, reset
  Demultiplexer #(.enable("false")) demultiplexer_2 (
    .out0(demultiplexer_2_out0), .out1(L_i2), .in(IDLE_q), .sel(End_CU));
  Copy copy_1 (
    .CLK(CLK), .Start(demultiplexer_1_out1), .i____len(i____len), .L_i(L_i0), .S_i(S_i0), .Write(Write0),
    .L_len(L_len), .RST_i(RST_i), .End(copy_1_end));
  or or_2 (or_2_out, L_i2, d_ff_7_q);
  D_Flip_Flop d_ff_2 (.clk(CLK), .D(or_2_out), .Q(d_ff_2_q));  // open: Qn, preset, en, reset
  Demultiplexer #(.enable("false")) demultiplexer_3 (
    .out0(demultiplexer_3_out0), .out1(demultiplexer_3_out1), .in(d_ff_2_q), .sel(i____len));
  Control_Unit control_unit_1 (
    .CLK(CLK), .Start(copy_1_end), .i___len(i___len), .j___len___i___1(j___len___i___1),
    .A___j_____A___j___1(A__j_____A__j___1), .End(End_CU), .L_i(L_i1), .S_i(S_i1), .L_j(L_j), .S_j(S_j),
    .Write(Write1), .L_A__j(L_A__j), .L_A__j___1(L_A__j___1), .out_14(S_DM), .out_15(S_MO));
  or or_3 (or_3_out, demultiplexer_4_out0, demultiplexer_3_out0);
  D_Flip_Flop d_ff_3 (.clk(CLK), .D(demultiplexer_3_out1), .Q(d_ff_3_q));  // open: Qn, preset, en, reset
  D_Flip_Flop d_ff_4 (.clk(CLK), .D(or_3_out), .Q(END));  // open: Qn, preset, en, reset
  D_Flip_Flop d_ff_5 (.clk(CLK), .D(d_ff_3_q), .Q(d_ff_5_q));  // open: Qn, preset, en, reset
  or or_4 (L_i, L_i0, L_i1, L_i2, L_i3);
  Demultiplexer #(.enable("false")) demultiplexer_4 (
    .out0(demultiplexer_4_out0), .out1(ReStart), .in(END), .sel(Start));
  or or_5 (S_i, S_i0, S_i1, L_i3);
  or or_6 (Write, Write0, Write1);
  Data_Path data_path_1 (
    .S_Dir_Memory(S_DM), .S_Memory_Out(S_MO), .CLK(CLK), .L_j(L_j), .S_j(S_j), .L_i(L_i), .S_i(S_i),
    .RST_i(RST_i), .L_A___j(L_A__j), .L_A___j___1(L_A__j___1), .L_len(L_len), .Data_Input(Data_Input),
    .Memory_Input(Memory_Input), .j___len___i___1(j___len___i___1), .Dir_Memory(Dir_Memory),
    .A___j_____A___j___1(A__j_____A__j___1), .i___len(i___len), .i____len(i____len), .Lenght(len),
    .Memory_Out(Memory_Out));
  PRINT_DEC print_dec_1 (
    .num(Memory_Input), .start(d_ff_5_q), .CLK(CLK), .RST(Start), .ASCII(ASCII), .Write_ASCII(W_ASCII),
    .END(L_i3));
  D_Flip_Flop d_ff_6 (.clk(CLK), .D(L_i3), .Q(d_ff_6_q));  // open: Qn, preset, en, reset
  D_Flip_Flop d_ff_7 (.clk(CLK), .D(d_ff_6_q), .Q(d_ff_7_q));  // open: Qn, preset, en, reset

  // Other names for the same wires on the sheet: DI[31:0] = Data_Input; DM[23:0] = Dir_Memory;
  //   MI[31:0] = Memory_Input; MO[31:0] = Memory_Out; S_i2 = L_i3
endmodule
