// Logisim project BigASM Polinomy.circ as structural Verilog
module BOARD_BIG_ASM (
  output out_1
);

  wire button_1_out, CLK, CLR, d_ff_1_q, not_1_out, Write, Write_ASCII;
  wire [6:0] ASCII;
  wire [7:0] counter_1_q;
  wire [23:0] Dir_INPUT, Dir_MEMORY;
  wire [31:0] INPUT, MEMORY_IN, MEMORY_OUT;

  Button button_1 (.out(button_1_out));
  Clock clock_1 (.out(CLK));
  D_Flip_Flop d_ff_1 (.clk(CLK), .D(1'b1), .Q(d_ff_1_q), .reset(button_1_out));  // open: Qn, preset, en
  D_Flip_Flop d_ff_2 (.clk(CLK), .D(d_ff_1_q), .Qn(CLR), .reset(button_1_out));  // open: Q, preset, en
  BIG_ASM big_asm_1 (
    .DATA_INPUT(INPUT), .MEMORY_IN(MEMORY_OUT), .CLK(CLK), .CLR(CLR), .DIR_INPUT(Dir_INPUT),
    .MEMORY_OUT(MEMORY_IN), .DIR_MEMORY(Dir_MEMORY), .Write_OUTPUT(Write), .ASCII(ASCII),
    .Write_ASCII(Write_ASCII), .END(out_1));
  MEMORY memory_1 (.DIR(Dir_MEMORY), .DATA_IN(MEMORY_IN), .WRITE(Write), .CLK(CLK), .CLR(CLR), .DATA_OUT(MEMORY_OUT));
  INPUT input_1 (.DIR(Dir_INPUT), .CLK(CLK), .DATA_OUT(INPUT));
  Counter counter_1 (.load(1'b0), .count(not_1_out), .Q(counter_1_q), .clk(CLK), .clr(CLR));  // open: D, carry
  not not_1 (not_1_out, out_1);
  // Probe on counter_1_q
  TTY #(.rows(32), .cols(60)) tty_1 (.data(ASCII), .clk(CLK), .we(Write_ASCII), .clr(CLR));

  // Other names for the same wires on the sheet: END = out_1

  // Notes on the sheet:
  //   COUNTER
  //   BOARD
endmodule

module INPUT (
  input  [23:0] DIR,
  input  CLK,
  output [31:0] DATA_OUT
);

  RAM #(.addrWidth(24), .dataWidth(32)) ram_1 (.addr(DIR), .data(DATA_OUT), .clk(CLK), .ld(1'b1));  // open: sel, clr
endmodule

module MEMORY (
  input  [23:0] DIR,
  input  [31:0] DATA_IN,
  input  WRITE,
  input  CLK,
  input  CLR,
  output [31:0] DATA_OUT
);

  RAM #(.addrWidth(24), .dataWidth(32), .bus("separate")) ram_1 (
    .addr(DIR), .din(DATA_IN), .data(DATA_OUT), .str(WRITE), .clk(CLK), .clr(CLR));  // open: sel, ld
endmodule

module BIG_ASM (
  input  [31:0] DATA_INPUT,
  input  [31:0] MEMORY_IN,
  input  CLK,
  input  CLR,
  output [23:0] DIR_INPUT,
  output [6:0] ASCII,
  output [31:0] MEMORY_OUT,
  output Write_ASCII,
  output END,
  output [23:0] DIR_MEMORY,
  output Write_OUTPUT
);

  Polinomy polinomy_1 (
    .CLK(CLK), .A__Index(DATA_INPUT), .Start(CLR), .Index(DIR_INPUT), .ASCII(ASCII), .W_ASCII(Write_ASCII),
    .END(END));

  // Other names for the same wires on the sheet: DI[31:0] = DATA_INPUT; Index[23:0] = DIR_INPUT; MI[31:0] = MEMORY_IN;
  //   Start = CLR
endmodule

module PRINT_UDEC (
  input  [31:0] num,
  input  start,
  input  CLK,
  input  RST,
  output [6:0] ASCII,
  output Write_ASCII,
  output \end 
);

  wire _0_c, _0_n, demultiplexer_1_out0, demultiplexer_2_out0, demultiplexer_2_out1, demultiplexer_3_out0,
       demultiplexer_3_out1, IDLE_2_q, IDLE_3_q, IDLE_4_q, IDLE_q, Lc, Lc_0, Ln, Ln_0, or_1_out;
  wire [23:0] bit_extender_1_out;
  wire [31:0] c, c___1, c___1_t, divider_1_rem, memory_1_data_out, multiplexer_1_out, multiplexer_2_out,
       multiplexer_3_out, n, n___10, n___10___48;

  Multiplexer #(.width(32), .enable("false")) multiplexer_1 (
    .in0(num), .in1(n___10), .out(multiplexer_1_out), .sel(Lc_0));
  Divider #(.width(32)) divider_1 (.a(n), .b(32'ha), .out(n___10), .rem(divider_1_rem));  // open: upper
  Adder #(.width(32)) adder_1 (.a(divider_1_rem), .b(32'h30), .out(n___10___48));  // open: cin, cout
  or or_1 (or_1_out, demultiplexer_1_out0, \end );
  Register #(.width(32)) u_n (.D(multiplexer_1_out), .en(Ln), .Q(n), .clk(CLK), .clr(RST));
  D_Flip_Flop IDLE (.clk(CLK), .D(or_1_out), .Q(IDLE_q), .preset(RST));  // open: Qn, en, reset
  Demultiplexer #(.enable("false")) demultiplexer_1 (
    .out0(demultiplexer_1_out0), .out1(Ln_0), .in(IDLE_q), .sel(start));
  or or_2 (Write_ASCII, demultiplexer_3_out0, demultiplexer_2_out1);
  Multiplexer #(.width(32), .enable("false")) multiplexer_2 (
    .in0(c___1), .in1(c___1_t), .out(multiplexer_2_out), .sel(Write_ASCII));
  Adder #(.width(32)) adder_2 (.a(c), .b(32'h1), .out(c___1));  // open: cin, cout
  Subtractor #(.width(32)) subtractor_1 (.a(c), .b(32'h1), .out(c___1_t));  // open: bin, bout
  D_Flip_Flop IDLE_2 (.clk(CLK), .D(Ln_0), .Q(IDLE_2_q), .reset(RST));  // open: Qn, preset, en
  Register #(.width(32)) u_c (.D(multiplexer_2_out), .en(Lc), .Q(c), .clk(CLK), .clr(RST));
  or or_3 (Lc_0, IDLE_2_q, demultiplexer_3_out1);
  Multiplexer #(.width(32), .enable("false")) multiplexer_3 (
    .in0(c), .in1(c___1_t), .out(multiplexer_3_out), .sel(Write_ASCII));
  Comparator #(.width(32), .mode("unsigned")) comparator_1 (.a({32{1'b0}}), .b(n), .lt(_0_n));  // open: gt, eq
  Comparator #(.width(32), .mode("unsigned")) comparator_2 (.a({32{1'b0}}), .b(c), .lt(_0_c));  // open: gt, eq
  D_Flip_Flop IDLE_3 (.clk(CLK), .D(Write_ASCII), .Q(IDLE_3_q), .reset(RST));  // open: Qn, preset, en
  Demultiplexer #(.enable("false")) demultiplexer_2 (
    .out0(demultiplexer_2_out0), .out1(demultiplexer_2_out1), .in(IDLE_3_q), .sel(_0_c));
  Bit_Extender #(.in_width(32), .out_width(24)) bit_extender_1 (.in(multiplexer_3_out), .out(bit_extender_1_out));
  D_Flip_Flop IDLE_4 (.clk(CLK), .D(Lc_0), .Q(IDLE_4_q), .reset(RST));  // open: Qn, preset, en
  or or_4 (Lc, Lc_0, Write_ASCII);
  or or_5 (Ln, Ln_0, Lc_0);
  Demultiplexer #(.enable("false")) demultiplexer_3 (
    .out0(demultiplexer_3_out0), .out1(demultiplexer_3_out1), .in(IDLE_4_q), .sel(_0_n));
  D_Flip_Flop IDLE_5 (.clk(CLK), .D(demultiplexer_2_out0), .Q(\end ), .reset(RST));  // open: Qn, preset, en
  MEMORY memory_1 (
    .DIR(bit_extender_1_out), .DATA_IN(n___10___48), .WRITE(Lc_0), .CLK(CLK), .CLR(RST),
    .DATA_OUT(memory_1_data_out));
  Bit_Extender #(.in_width(32), .out_width(7)) bit_extender_2 (.in(memory_1_data_out), .out(ASCII));

  // Other names for the same wires on the sheet: Lc_1 = Write_ASCII; Sc = Write_ASCII; Ln_1 = Lc_0; Sn = Lc_0;
  //   Write = Lc_0
endmodule

module PRINT_DEC (
  input  [31:0] num,
  input  start,
  input  CLK,
  input  RST,
  output [6:0] ASCII,
  output Write_ASCII,
  output END
);

  wire demultiplexer_1_out0, demultiplexer_1_out1, demultiplexer_2_out0, demultiplexer_3_out0, end_t,
       IDLE_3_q, IDLE_q, or_1_out, or_2_out, or_3_out, S_ASCII, startUDEC, Write_ASCII_1;
  wire [6:0] ASCII_t;
  wire [31:0] multiplexer_1_out, negator_1_out;

  or or_1 (or_1_out, demultiplexer_1_out0, END);
  Negator #(.width(32)) negator_1 (.in(num), .out(negator_1_out));
  D_Flip_Flop IDLE (.clk(CLK), .D(or_1_out), .Q(IDLE_q), .preset(RST));  // open: Qn, en, reset
  Demultiplexer #(.enable("false")) demultiplexer_1 (
    .out0(demultiplexer_1_out0), .out1(demultiplexer_1_out1), .in(IDLE_q), .sel(start));
  Multiplexer #(.width(32), .enable("false")) multiplexer_1 (
    .in0(num), .in1(negator_1_out), .out(multiplexer_1_out), .sel(num[31]));
  Demultiplexer #(.enable("false")) demultiplexer_2 (
    .out0(demultiplexer_2_out0), .out1(S_ASCII), .in(demultiplexer_1_out1), .sel(num[31]));
  or or_2 (or_2_out, demultiplexer_2_out0, S_ASCII);
  D_Flip_Flop IDLE_2 (.clk(CLK), .D(or_2_out), .Q(startUDEC), .reset(RST));  // open: Qn, preset, en
  PRINT_UDEC print_udec_1 (
    .num(multiplexer_1_out), .start(startUDEC), .CLK(CLK), .RST(RST), .ASCII(ASCII_t),
    .Write_ASCII(Write_ASCII_1), .\end (end_t));
  D_Flip_Flop IDLE_3 (.clk(CLK), .D(or_3_out), .Q(IDLE_3_q), .reset(RST));  // open: Qn, preset, en
  or or_3 (or_3_out, startUDEC, demultiplexer_3_out0);
  Demultiplexer #(.enable("false")) demultiplexer_3 (
    .out0(demultiplexer_3_out0), .out1(END), .in(IDLE_3_q), .sel(end_t));
  Multiplexer #(.width(7), .enable("false")) multiplexer_2 (
    .in0(ASCII_t), .in1(7'b0101101), .out(ASCII), .sel(S_ASCII));
  or or_4 (Write_ASCII, S_ASCII, Write_ASCII_1);

  // Other names for the same wires on the sheet: sign = num[31]; Write_ASCII_0 = S_ASCII
endmodule

module TEST_PRINT (
  input  [31:0] in_1,
  output out_2
);

  wire button_1_out, button_2_out, CLK, CLR, d_ff_1_q, Write_ASCII;
  wire [6:0] ASCII;

  Button button_1 (.out(button_1_out));
  Clock clock_1 (.out(CLK));
  D_Flip_Flop d_ff_1 (.clk(CLK), .D(1'b1), .Q(d_ff_1_q), .reset(button_1_out));  // open: Qn, preset, en
  D_Flip_Flop d_ff_2 (.clk(CLK), .D(d_ff_1_q), .Qn(CLR), .reset(button_1_out));  // open: Q, preset, en
  Button button_2 (.out(button_2_out));
  PRINT_UDEC print_udec_1 ();  // open: num, start, CLK, RST, ASCII, Write_ASCII, end
  PRINT_DEC print_dec_1 (
    .num(in_1), .start(button_2_out), .CLK(CLK), .RST(CLR), .ASCII(ASCII), .Write_ASCII(Write_ASCII),
    .END(out_2));
  TTY #(.rows(32), .cols(60)) tty_1 (.data(ASCII), .clk(CLK), .we(Write_ASCII), .clr(CLR));
endmodule

module Data_Path (
  input  CLK,
  input  S_Result,
  input  L_Result,
  input  RST_Result,
  input  [31:0] Data_Input,
  input  L_X,
  input  L_Index,
  input  RST_Index,
  input  S_Pow,
  input  L_Pow,
  input  L_len,
  output [31:0] out_12,
  output [23:0] out_13,
  output out_14
);

  wire [23:0] Index___1;
  wire [31:0] adder_1_out, bit_extender_1_out, len, multiplexer_1_out, multiplexer_2_out, multiplier_1_out,
       Pow, Pow___X, Result___A__Index, Result___Pow___A__Index, X;

  Multiplexer #(.width(32), .enable("false")) multiplexer_1 (
    .in0(Result___A__Index), .in1(Result___Pow___A__Index), .out(multiplexer_1_out), .sel(S_Result));
  Register #(.width(32)) Result (.D(multiplexer_1_out), .en(L_Result), .Q(out_12), .clk(CLK), .clr(RST_Result));
  Multiplier #(.width(32)) multiplier_1 (.a(Pow), .b(Data_Input), .out(multiplier_1_out));  // open: cin, cout
  Adder #(.width(32)) adder_1 (.a(len), .b(32'h2), .out(adder_1_out));  // open: cin, cout
  Adder #(.width(24)) adder_2 (.a(out_13), .b(24'h1), .out(Index___1));  // open: cin, cout
  Adder #(.width(32)) adder_3 (.a(Data_Input), .b(out_12), .out(Result___A__Index));  // open: cin, cout
  assign bit_extender_1_out = {{8{1'b0}}, out_13};  // Bit_Extender bit_extender_1
  Comparator #(.width(32), .mode("unsigned")) comparator_1 (
    .a(bit_extender_1_out), .b(adder_1_out), .lt(out_14));  // open: gt, eq
  Register #(.width(24)) Index (.D(Index___1), .en(L_Index), .Q(out_13), .clk(CLK), .clr(RST_Index));
  Adder #(.width(32)) adder_4 (.a(multiplier_1_out), .b(out_12), .out(Result___Pow___A__Index));  // open: cin, cout
  Register #(.width(32)) register_1 (.D(Data_Input), .en(L_len), .Q(len), .clk(CLK));  // open: clr
  Multiplier #(.width(32)) multiplier_2 (.a(Pow), .b(X), .out(Pow___X));  // open: cin, cout
  Register #(.width(32)) u_Pow (.D(multiplexer_2_out), .en(L_Pow), .Q(Pow), .clk(CLK));  // open: clr
  Multiplexer #(.width(32), .enable("false")) multiplexer_2 (
    .in0(X), .in1(Pow___X), .out(multiplexer_2_out), .sel(S_Pow));
  Register #(.width(32)) u_X (.D(Data_Input), .en(L_X), .Q(X), .clk(CLK));  // open: clr

  // Other names for the same wires on the sheet: A__Index[31:0] = Data_Input; Index[23:0] = out_13;
  //   Index___len = out_14; Result[31:0] = out_12
endmodule

module Control_Unit (
  input  CLK,
  input  Start,
  input  Index___len,
  output out_4,
  output out_5,
  output out_6,
  output out_7,
  output out_8,
  output out_9,
  output out_10,
  output out_11,
  output out_12,
  output out_13
);

  wire d_ff_1_q, d_ff_3_q, demultiplexer_1_out0, demultiplexer_3_out0, demultiplexer_3_out1, End_q, IDLE_q,
       L_Index1, or_1_out, or_5_out, or_6_out, While_q;

  or or_1 (or_1_out, demultiplexer_1_out0, demultiplexer_3_out1);
  D_Flip_Flop IDLE (.clk(CLK), .D(or_1_out), .Q(IDLE_q), .preset(Start));  // open: Qn, en, reset
  Demultiplexer #(.enable("false")) demultiplexer_1 (
    .out0(demultiplexer_1_out0), .out1(out_4), .in(IDLE_q), .sel(Start));
  D_Flip_Flop d_ff_1 (.clk(CLK), .D(out_4), .Q(d_ff_1_q));  // open: Qn, preset, en, reset
  D_Flip_Flop d_ff_2 (.clk(CLK), .D(d_ff_1_q), .Q(out_8));  // open: Qn, preset, en, reset
  D_Flip_Flop d_ff_3 (.clk(CLK), .D(out_8), .Q(d_ff_3_q));  // open: Qn, preset, en, reset
  D_Flip_Flop d_ff_4 (.clk(CLK), .D(d_ff_3_q), .Q(L_Index1));  // open: Qn, preset, en, reset
  or or_2 (out_7, out_11, out_8, L_Index1);
  or or_3 (out_9, L_Index1, out_11);
  or or_4 (out_10, L_Index1, out_11);
  or or_5 (or_5_out, L_Index1, out_11);
  D_Flip_Flop While (.clk(CLK), .D(or_5_out), .Q(While_q));  // open: Qn, preset, en, reset
  Demultiplexer #(.enable("false")) demultiplexer_2 (.out0(out_13), .out1(out_11), .in(While_q), .sel(Index___len));
  or or_6 (or_6_out, demultiplexer_3_out0, out_13);
  D_Flip_Flop End (.clk(CLK), .D(or_6_out), .Q(End_q));  // open: Qn, preset, en, reset
  Demultiplexer #(.enable("false")) demultiplexer_3 (
    .out0(demultiplexer_3_out0), .out1(demultiplexer_3_out1), .in(End_q), .sel(Start));

  assign out_5 = out_4;
  assign out_6 = out_4;
  assign out_12 = out_11;

  // Other names for the same wires on the sheet: End = out_13; L_Index = out_7; L_Index0 = out_8; L_len = out_8;
  //   L_Pow = out_10; L_Result = out_9; L_Pow0 = L_Index1; L_Result0 = L_Index1; L_X = out_4; RST_Index = out_4;
  //   RST_Result = out_4; L_Index3 = out_11; L_Pow1 = out_11; L_Result1 = out_11; S_Pow = out_11; S_Result = out_11
endmodule

module Polinomy (
  input  CLK,
  input  [31:0] A__Index,
  input  Start,
  output [23:0] Index,
  output [6:0] ASCII,
  output W_ASCII,
  output END
);

  wire control_unit_1_out_4, control_unit_1_out_5, control_unit_1_out_6, control_unit_1_out_7,
       control_unit_1_out_8, control_unit_1_out_9, control_unit_1_out_10, control_unit_1_out_11,
       control_unit_1_out_12, d_ff_1_q, demultiplexer_1_out0, demultiplexer_1_out1, demultiplexer_2_out0,
       End_t, I_L, or_1_out, or_2_out, print_udec_1_end, ReStart;
  wire [31:0] Result;

  D_Flip_Flop d_ff_1 (.clk(CLK), .D(or_1_out), .Q(d_ff_1_q), .preset(Start));  // open: Qn, en, reset
  or or_1 (or_1_out, demultiplexer_1_out0, ReStart);
  Demultiplexer #(.enable("false")) demultiplexer_1 (
    .out0(demultiplexer_1_out0), .out1(demultiplexer_1_out1), .in(d_ff_1_q), .sel(Start));
  PRINT_UDEC print_udec_1 (
    .num(Result), .start(End_t), .CLK(CLK), .RST(Start), .ASCII(ASCII), .Write_ASCII(W_ASCII),
    .\end (print_udec_1_end));
  or or_2 (or_2_out, print_udec_1_end, demultiplexer_2_out0);
  D_Flip_Flop d_ff_2 (.clk(CLK), .D(or_2_out), .Q(END));  // open: Qn, preset, en, reset
  Demultiplexer #(.enable("false")) demultiplexer_2 (
    .out0(demultiplexer_2_out0), .out1(ReStart), .in(END), .sel(Start));
  Control_Unit control_unit_1 (
    .CLK(CLK), .Start(demultiplexer_1_out1), .Index___len(I_L), .out_4(control_unit_1_out_4),
    .out_5(control_unit_1_out_5), .out_6(control_unit_1_out_6), .out_7(control_unit_1_out_7),
    .out_8(control_unit_1_out_8), .out_9(control_unit_1_out_9), .out_10(control_unit_1_out_10),
    .out_11(control_unit_1_out_11), .out_12(control_unit_1_out_12), .out_13(End_t));
  Data_Path data_path_1 (
    .CLK(CLK), .S_Result(control_unit_1_out_12), .L_Result(control_unit_1_out_9),
    .RST_Result(control_unit_1_out_5), .Data_Input(A__Index), .L_X(control_unit_1_out_4),
    .L_Index(control_unit_1_out_7), .RST_Index(control_unit_1_out_6), .S_Pow(control_unit_1_out_11),
    .L_Pow(control_unit_1_out_10), .L_len(control_unit_1_out_8), .out_12(Result), .out_13(Index), .out_14(I_L));
endmodule
