// Logisim project BigASM StrongBranch.circ as structural Verilog
module BOARD_BIG_ASM (
  output out_1
);

  wire button_1_out, CLK, CLR, d_ff_1_q, not_1_out, Write, Write_ASCII;
  wire [6:0] ASCII;
  wire [7:0] counter_1_q;
  wire [23:0] Dir_INPUT, Dir_MEMORY;
  wire [31:0] INPUT, MEMORY_IN, MEMORY_OUT;

  Button button_1 (.out(button_1_out));
  Clock clock_1 (.out(CLK));
  D_Flip_Flop d_ff_1 (.clk(CLK), .D(1'b1), .Q(d_ff_1_q), .reset(button_1_out));  // open: Qn, preset, en
  D_Flip_Flop d_ff_2 (.clk(CLK), .D(d_ff_1_q), .Qn(CLR), .reset(button_1_out));  // open: Q, preset, en
  BIG_ASM big_asm_1 (
    .DATA_INPUT(INPUT), .MEMORY_IN(MEMORY_OUT), .CLK(CLK), .CLR(CLR), .DIR_INPUT(Dir_INPUT),
    .MEMORY_OUT(MEMORY_IN), .DIR_MEMORY(Dir_MEMORY), .Write_OUTPUT(Write), .ASCII(ASCII),
    .Write_ASCII(Write_ASCII), .END(out_1));
  MEMORY memory_1 (.DIR(Dir_MEMORY), .DATA_IN(MEMORY_IN), .WRITE(Write), .CLK(CLK), .CLR(CLR), .DATA_OUT(MEMORY_OUT));
  INPUT input_1 (.DIR(Dir_INPUT), .CLK(CLK), .DATA_OUT(INPUT));
  Counter counter_1 (.load(1'b0), .count(not_1_out), .Q(counter_1_q), .clk(CLK), .clr(CLR));  // open: D, carry
  not not_1 (not_1_out, out_1);
  // Probe on counter_1_q
  TTY #(.rows(32), .cols(60)) tty_1 (.data(ASCII), .clk(CLK), .we(Write_ASCII), .clr(CLR));

  // Other names for the same wires on the sheet: END = out_1

  // Notes on the sheet:
  //   COUNTER
  //   BOARD
endmodule

module INPUT (
  input  [23:0] DIR,
  input  CLK,
  output [31:0] DATA_OUT
);

  RAM #(.addrWidth(24), .dataWidth(32)) ram_1 (.addr(DIR), .data(DATA_OUT), .clk(CLK), .ld(1'b1));  // open: sel, clr
endmodule

module MEMORY (
  input  [23:0] DIR,
  input  [31:0] DATA_IN,
  input  WRITE,
  input  CLK,
  input  CLR,
  output [31:0] DATA_OUT
);

  RAM #(.addrWidth(24), .dataWidth(32), .bus("separate")) ram_1 (
    .addr(DIR), .din(DATA_IN), .data(DATA_OUT), .str(WRITE), .clk(CLK), .clr(CLR));  // open: sel, ld
endmodule

module BIG_ASM (
  input  [31:0] DATA_INPUT,
  input  [31:0] MEMORY_IN,
  input  CLK,
  input  CLR,
  output [23:0] DIR_INPUT,
  output [6:0] ASCII,
  output Write_ASCII,
  output [31:0] MEMORY_OUT,
  output [23:0] DIR_MEMORY,
  output END,
  output Write_OUTPUT
);

  StrongBranch strongbranch_1 (
    .CLK(CLK), .Start(CLR), .Memory_Input(MEMORY_IN), .Data_Input(DATA_INPUT), .ASCII(ASCII),
    .W_ASCII(Write_ASCII), .MO(MEMORY_OUT), .DM(DIR_INPUT), .END(END), .Write(Write_OUTPUT));

  assign DIR_MEMORY = DIR_INPUT;

  // Other names for the same wires on the sheet: DI[31:0] = DATA_INPUT; DM[23:0] = DIR_INPUT; MI[31:0] = MEMORY_IN;
  //   MO[31:0] = MEMORY_OUT; Write = Write_OUTPUT
endmodule

module PRINT_UDEC (
  input  [31:0] num,
  input  start,
  input  CLK,
  input  RST,
  output [6:0] ASCII,
  output Write_ASCII,
  output \end 
);

  wire _0_c, _0_n, demultiplexer_1_out0, demultiplexer_2_out0, demultiplexer_2_out1, demultiplexer_3_out0,
       demultiplexer_3_out1, IDLE_2_q, IDLE_3_q, IDLE_4_q, IDLE_q, Lc, Lc_0, Ln, Ln_0, or_1_out;
  wire [23:0] bit_extender_1_out;
  wire [31:0] c, c___1, c___1_t, divider_1_rem, memory_1_data_out, multiplexer_1_out, multiplexer_2_out,
       multiplexer_3_out, n, n___10, n___10___48;

  Multiplexer #(.width(32), .enable("false")) multiplexer_1 (
    .in0(num), .in1(n___10), .out(multiplexer_1_out), .sel(Lc_0));
  Divider #(.width(32)) divider_1 (.a(n), .b(32'ha), .out(n___10), .rem(divider_1_rem));  // open: upper
  Adder #(.width(32)) adder_1 (.a(divider_1_rem), .b(32'h30), .out(n___10___48));  // open: cin, cout
  or or_1 (or_1_out, demultiplexer_1_out0, \end );
  Register #(.width(32)) u_n (.D(multiplexer_1_out), .en(Ln), .Q(n), .clk(CLK), .clr(RST));
  D_Flip_Flop IDLE (.clk(CLK), .D(or_1_out), .Q(IDLE_q), .preset(RST));  // open: Qn, en, reset
  Demultiplexer #(.enable("false")) demultiplexer_1 (
    .out0(demultiplexer_1_out0), .out1(Ln_0), .in(IDLE_q), .sel(start));
  or or_2 (Write_ASCII, demultiplexer_3_out0, demultiplexer_2_out1);
  Multiplexer #(.width(32), .enable("false")) multiplexer_2 (
    .in0(c___1), .in1(c___1_t), .out(multiplexer_2_out), .sel(Write_ASCII));
  Adder #(.width(32)) adder_2 (.a(c), .b(32'h1), .out(c___1));  // open: cin, cout
  Subtractor #(.width(32)) subtractor_1 (.a(c), .b(32'h1), .out(c___1_t));  // open: bin, bout
  D_Flip_Flop IDLE_2 (.clk(CLK), .D(Ln_0), .Q(IDLE_2_q), .reset(RST));  // open: Qn, preset, en
  Register #(.width(32)) u_c (.D(multiplexer_2_out), .en(Lc), .Q(c), .clk(CLK), .clr(RST));
  or or_3 (Lc_0, IDLE_2_q, demultiplexer_3_out1);
  Multiplexer #(.width(32), .enable("false")) multiplexer_3 (
    .in0(c), .in1(c___1_t), .out(multiplexer_3_out), .sel(Write_ASCII));
  Comparator #(.width(32), .mode("unsigned")) comparator_1 (.a({32{1'b0}}), .b(n), .lt(_0_n));  // open: gt, eq
  Comparator #(.width(32), .mode("unsigned")) comparator_2 (.a({32{1'b0}}), .b(c), .lt(_0_c));  // open: gt, eq
  D_Flip_Flop IDLE_3 (.clk(CLK), .D(Write_ASCII), .Q(IDLE_3_q), .reset(RST));  // open: Qn, preset, en
  Demultiplexer #(.enable("false")) demultiplexer_2 (
    .out0(demultiplexer_2_out0), .out1(demultiplexer_2_out1), .in(IDLE_3_q), .sel(_0_c));
  Bit_Extender #(.in_width(32), .out_width(24)) bit_extender_1 (.in(multiplexer_3_out), .out(bit_extender_1_out));
  D_Flip_Flop IDLE_4 (.clk(CLK), .D(Lc_0), .Q(IDLE_4_q), .reset(RST));  // open: Qn, preset, en
  or or_4 (Lc, Lc_0, Write_ASCII);
  or or_5 (Ln, Ln_0, Lc_0);
  Demultiplexer #(.enable("false")) demultiplexer_3 (
    .out0(demultiplexer_3_out0), .out1(demultiplexer_3_out1), .in(IDLE_4_q), .sel(_0_n));
  D_Flip_Flop IDLE_5 (.clk(CLK), .D(demultiplexer_2_out0), .Q(\end ), .reset(RST));  // open: Qn, preset, en
  MEMORY memory_1 (
    .DIR(bit_extender_1_out), .DATA_IN(n___10___48), .WRITE(Lc_0), .CLK(CLK), .CLR(RST),
    .DATA_OUT(memory_1_data_out));
  Bit_Extender #(.in_width(32), .out_width(7)) bit_extender_2 (.in(memory_1_data_out), .out(ASCII));

  // Other names for the same wires on the sheet: Lc_1 = Write_ASCII; Sc = Write_ASCII; Ln_1 = Lc_0; Sn = Lc_0;
  //   Write = Lc_0
endmodule

module PRINT_DEC (
  input  [31:0] num,
  input  start,
  input  CLK,
  input  RST,
  output [6:0] ASCII,
  output Write_ASCII,
  output END
);

  wire demultiplexer_1_out0, demultiplexer_1_out1, demultiplexer_2_out0, demultiplexer_3_out0, end_t,
       IDLE_3_q, IDLE_q, or_1_out, or_2_out, or_3_out, S_ASCII, startUDEC, Write_ASCII_1;
  wire [6:0] ASCII_t;
  wire [31:0] multiplexer_1_out, negator_1_out;

  or or_1 (or_1_out, demultiplexer_1_out0, END);
  Negator #(.width(32)) negator_1 (.in(num), .out(negator_1_out));
  D_Flip_Flop IDLE (.clk(CLK), .D(or_1_out), .Q(IDLE_q), .preset(RST));  // open: Qn, en, reset
  Demultiplexer #(.enable("false")) demultiplexer_1 (
    .out0(demultiplexer_1_out0), .out1(demultiplexer_1_out1), .in(IDLE_q), .sel(start));
  Multiplexer #(.width(32), .enable("false")) multiplexer_1 (
    .in0(num), .in1(negator_1_out), .out(multiplexer_1_out), .sel(num[31]));
  Demultiplexer #(.enable("false")) demultiplexer_2 (
    .out0(demultiplexer_2_out0), .out1(S_ASCII), .in(demultiplexer_1_out1), .sel(num[31]));
  or or_2 (or_2_out, demultiplexer_2_out0, S_ASCII);
  D_Flip_Flop IDLE_2 (.clk(CLK), .D(or_2_out), .Q(startUDEC), .reset(RST));  // open: Qn, preset, en
  PRINT_UDEC print_udec_1 (
    .num(multiplexer_1_out), .start(startUDEC), .CLK(CLK), .RST(RST), .ASCII(ASCII_t),
    .Write_ASCII(Write_ASCII_1), .\end (end_t));
  D_Flip_Flop IDLE_3 (.clk(CLK), .D(or_3_out), .Q(IDLE_3_q), .reset(RST));  // open: Qn, preset, en
  or or_3 (or_3_out, startUDEC, demultiplexer_3_out0);
  Demultiplexer #(.enable("false")) demultiplexer_3 (
    .out0(demultiplexer_3_out0), .out1(END), .in(IDLE_3_q), .sel(end_t));
  Multiplexer #(.width(7), .enable("false")) multiplexer_2 (
    .in0(ASCII_t), .in1(7'b0101101), .out(ASCII), .sel(S_ASCII));
  or or_4 (Write_ASCII, S_ASCII, Write_ASCII_1);

  // Other names for the same wires on the sheet: sign = num[31]; Write_ASCII_0 = S_ASCII
endmodule

module TEST_PRINT (
  input  [31:0] in_1,
  output out_2
);

  wire button_1_out, button_2_out, CLK, CLR, d_ff_1_q, Write_ASCII;
  wire [6:0] ASCII;

  Button button_1 (.out(button_1_out));
  Clock clock_1 (.out(CLK));
  D_Flip_Flop d_ff_1 (.clk(CLK), .D(1'b1), .Q(d_ff_1_q), .reset(button_1_out));  // open: Qn, preset, en
  D_Flip_Flop d_ff_2 (.clk(CLK), .D(d_ff_1_q), .Qn(CLR), .reset(button_1_out));  // open: Q, preset, en
  Button button_2 (.out(button_2_out));
  PRINT_UDEC print_udec_1 ();  // open: num, start, CLK, RST, ASCII, Write_ASCII, end
  PRINT_DEC print_dec_1 (
    .num(in_1), .start(button_2_out), .CLK(CLK), .RST(CLR), .ASCII(ASCII), .Write_ASCII(Write_ASCII),
    .END(out_2));
  TTY #(.rows(32), .cols(60)) tty_1 (.data(ASCII), .clk(CLK), .we(Write_ASCII), .clr(CLR));
endmodule

module Data_Path (
  input  CLK,
  input  S_Index,
  input  [1:0] S_Dir_Memory,
  input  RST_Max,
  input  S_Memory_Out,
  input  [31:0] Memory_Input,
  input  L_K,
  input  L_Aux,
  input  [31:0] Data_Input,
  input  L_Index,
  input  L_A__Index,
  input  L_Max,
  input  L_A_____Index___1_____2___1,
  output A__Index_____Max___A__Index_____K,
  output Index___2,
  output Index____1,
  output A__Index_____0,
  output [23:0] Dir_Memory,
  output [31:0] Memory_Out,
  output [31:0] Max
);

  wire comparator_1_gt, comparator_2_lt, comparator_4_eq;
  wire [23:0] adder_1_out, bit_extender_1_out, Index, Index___1_____2, Index_minus_minus, Index_plus_plus,
       len___1, multiplexer_1_out;
  wire [31:0] A_____Index___1_____2, A_____Index___1_____2_____A__Index_____DI, A___Index_____DI, A__Index,
       Aux, K;

  Multiplexer #(.width(24), .enable("false")) multiplexer_1 (
    .in0(len___1), .in1(Index_minus_minus), .out(multiplexer_1_out), .sel(S_Index));
  Register #(.width(24)) u_Index (.D(multiplexer_1_out), .en(L_Index), .Q(Index), .clk(CLK));  // open: clr
  Adder #(.width(24)) adder_1 (.a(Index), .b(24'h1), .out(adder_1_out));  // open: cin, cout
  Adder #(.width(32)) adder_2 (
    .a(A_____Index___1_____2), .b(Aux), .out(A_____Index___1_____2_____A__Index_____DI));  // open: cin, cout
  Divider #(.width(24)) divider_1 (.a(adder_1_out), .b(24'h2), .out(Index___1_____2));  // open: upper, rem
  Register #(.width(32)) u_A__Index (.D(Memory_Input), .en(L_A__Index), .Q(A__Index), .clk(CLK));  // open: clr
  Register #(.width(32)) u_Aux (.D(A___Index_____DI), .en(L_Aux), .Q(Aux), .clk(CLK));  // open: clr
  Register #(.width(32)) u_Max (.D(Memory_Input), .en(L_Max), .Q(Max), .clk(CLK), .clr(RST_Max));
  Subtractor #(.width(24)) subtractor_1 (.a(Index), .b(24'h1), .out(Index_minus_minus));  // open: bin, bout
  Adder #(.width(24)) adder_3 (.a(Index), .b(24'h1), .out(Index_plus_plus));  // open: cin, cout
  Adder #(.width(32)) adder_4 (.a(A__Index), .b(Data_Input), .out(A___Index_____DI));  // open: cin, cout
  Register #(.width(32)) u_A_____Index___1_____2 (
    .D(Memory_Input), .en(L_A_____Index___1_____2___1), .Q(A_____Index___1_____2), .clk(CLK));  // open: clr
  Comparator #(.width(32)) comparator_1 (.a(A__Index), .b(Max), .gt(comparator_1_gt));  // open: eq, lt
  and and_1 (A__Index_____Max___A__Index_____K, comparator_1_gt, comparator_2_lt);
  Comparator #(.width(32)) comparator_2 (.a(A__Index), .b(K), .lt(comparator_2_lt));  // open: gt, eq
  Bit_Extender #(.in_width(32), .out_width(24)) bit_extender_1 (.in(Data_Input), .out(bit_extender_1_out));
  Register #(.width(32)) u_K (.D(Data_Input), .en(L_K), .Q(K), .clk(CLK));  // open: clr
  Adder #(.width(24)) adder_5 (.a(bit_extender_1_out), .b(24'h1), .out(len___1));  // open: cin, cout
  Multiplexer #(.select(2), .width(24), .enable("false")) multiplexer_2 (
    .in0(Index), .in1(Index___1_____2), .in2(24'h1), .in3({24{1'b0}}), .out(Dir_Memory), .sel(S_Dir_Memory));
  Multiplexer #(.width(32), .enable("false")) multiplexer_3 (
    .in0(A___Index_____DI), .in1(A_____Index___1_____2_____A__Index_____DI), .out(Memory_Out),
    .sel(S_Memory_Out));
  Comparator #(.width(32)) comparator_3 (.a(Data_Input), .b({32{1'b0}}), .gt(A__Index_____0));  // open: eq, lt
  Comparator #(.width(24)) comparator_4 (.a(Index), .b(24'h2), .gt(Index___2), .eq(comparator_4_eq));  // open: lt
  or or_1 (Index____1, Index___2, comparator_4_eq);

  // Other names for the same wires on the sheet: DI[31:0] = Data_Input; Index____2 = Index____1;
  //   L_A_____Index___1_____2 = L_A_____Index___1_____2___1; MI[31:0] = Memory_Input; S_DM[1:0] = S_Dir_Memory;
  //   S_MO = S_Memory_Out
endmodule

module Control_Unit (
  input  CLK,
  input  Start,
  input  Index___1,
  input  A__Index_____0,
  input  A__Index_____Max___A__Index_____K,
  input  Index____2,
  output End,
  output S_MO,
  output [1:0] S_DM,
  output Write,
  output L_A__Index,
  output L_A_____Index___1_____2,
  output S_Index,
  output L_Index,
  output L_Max,
  output L_K,
  output RST_Max,
  output L_Aux
);

  wire d_ff_1_q, d_ff_2_q, d_ff_2_qn, d_ff_3_q, d_ff_6_q, d_ff_9_q, d_ff_11_q, d_ff_12_q, d_ff_13_q,
       d_ff_14_q, demultiplexer_1_out0, demultiplexer_3_out0, demultiplexer_5_out0, demultiplexer_5_out1,
       demultiplexer_6_out0, L_A__Index__0, L_A__Index__1, L_A__Index__2, L_Index0, L_Index1, L_Index3,
       or_1_out, or_2_out, or_10_out, or_11_out, Write2;

  or or_1 (or_1_out, demultiplexer_1_out0, demultiplexer_5_out1);
  D_Flip_Flop d_ff_1 (.clk(CLK), .D(or_1_out), .Q(d_ff_1_q), .preset(Start));  // open: Qn, en, reset
  Demultiplexer #(.enable("false")) demultiplexer_1 (
    .out0(demultiplexer_1_out0), .out1(L_Index0), .in(d_ff_1_q), .sel(Start));
  or or_2 (or_2_out, d_ff_3_q, L_Index0);
  D_Flip_Flop #(.trigger("falling")) d_ff_2 (
    .clk(CLK), .D(or_2_out), .Q(d_ff_2_q), .Qn(d_ff_2_qn));  // open: preset, en, reset
  Demultiplexer #(.enable("false")) demultiplexer_2 (
    .out0(L_A__Index__1), .out1(L_A__Index__0), .in(d_ff_2_q), .sel(Index___1));
  D_Flip_Flop d_ff_3 (.clk(CLK), .D(L_Index1), .Q(d_ff_3_q));  // open: Qn, preset, en, reset
  D_Flip_Flop d_ff_4 (.clk(CLK), .D(L_A__Index__1), .Q(Write2));  // open: Qn, preset, en, reset
  D_Flip_Flop d_ff_5 (.clk(CLK), .D(Write2), .Q(L_K));  // open: Qn, preset, en, reset
  or or_3 (L_Index1, S_MO, demultiplexer_3_out0);
  D_Flip_Flop d_ff_6 (.clk(CLK), .D(L_A__Index__0), .Q(d_ff_6_q));  // open: Qn, preset, en, reset
  Demultiplexer #(.enable("false")) demultiplexer_3 (
    .out0(demultiplexer_3_out0), .out1(L_Aux), .in(d_ff_6_q), .sel(A__Index_____0));
  D_Flip_Flop d_ff_7 (.clk(CLK), .D(L_K), .Q(RST_Max));  // open: Qn, preset, en, reset
  or or_4 (S_DM[0], L_A_____Index___1_____2, L_K, S_MO);
  or or_5 (Write, L_Aux, S_MO, Write2);
  or or_6 (S_Index, L_Index1, L_Index3);
  or or_7 (S_DM[1], L_Index0, RST_Max, L_K);
  or or_8 (L_Index, L_Index0, L_Index1, RST_Max, L_Index3);
  or or_9 (L_A__Index, L_A__Index__0, L_A__Index__2, L_A__Index__1);
  D_Flip_Flop d_ff_8 (.clk(CLK), .D(L_Aux), .Q(L_A_____Index___1_____2));  // open: Qn, preset, en, reset
  D_Flip_Flop d_ff_9 (.clk(CLK), .D(L_A_____Index___1_____2), .Q(d_ff_9_q));  // open: Qn, preset, en, reset
  or or_10 (or_10_out, RST_Max, d_ff_12_q);
  D_Flip_Flop d_ff_10 (.clk(CLK), .D(d_ff_9_q), .Q(S_MO));  // open: Qn, preset, en, reset
  D_Flip_Flop d_ff_11 (.clk(CLK), .D(or_10_out), .Q(d_ff_11_q));  // open: Qn, preset, en, reset
  Demultiplexer #(.enable("false")) demultiplexer_4 (
    .out0(End), .out1(L_A__Index__2), .in(d_ff_11_q), .sel(Index____2));
  D_Flip_Flop d_ff_12 (.clk(CLK), .D(L_Index3), .Q(d_ff_12_q));  // open: Qn, preset, en, reset
  or or_11 (or_11_out, demultiplexer_5_out0, End);
  Demultiplexer #(.enable("false")) demultiplexer_5 (
    .out0(demultiplexer_5_out0), .out1(demultiplexer_5_out1), .in(d_ff_13_q), .sel(Start));
  D_Flip_Flop d_ff_13 (.clk(CLK), .D(or_11_out), .Q(d_ff_13_q));  // open: Qn, preset, en, reset
  D_Flip_Flop d_ff_14 (.clk(CLK), .D(L_A__Index__2), .Q(d_ff_14_q));  // open: Qn, preset, en, reset
  Demultiplexer #(.enable("false")) demultiplexer_6 (
    .out0(demultiplexer_6_out0), .out1(L_Max), .in(d_ff_14_q), .sel(A__Index_____Max___A__Index_____K));
  or or_12 (L_Index3, L_Max, demultiplexer_6_out0);

  // Other names for the same wires on the sheet: Index___2 = Index___1; S_DM00 = L_A_____Index___1_____2;
  //   S_DM10 = L_Index0; S_DM02 = L_K; S_DM11 = L_K; L_Index2 = RST_Max; S_DM12 = RST_Max; S_Index0 = L_Index1;
  //   S_Index1 = L_Index3; Write0 = L_Aux; S_DM01 = S_MO; Write1 = S_MO
endmodule

module StrongBranch (
  input  CLK,
  input  Start,
  input  [31:0] Memory_Input,
  input  [31:0] Data_Input,
  output [31:0] MO,
  output [6:0] ASCII,
  output W_ASCII,
  output END,
  output [23:0] DM,
  output Write
);

  wire A__Index_____0, A__Index_____Max___A__Index_____K, d_ff_1_q, demultiplexer_1_out0,
       demultiplexer_1_out1, demultiplexer_2_out0, End_CU, Index___2, Index____2, L_A____Index___1_____2,
       L_A__Index, L_Aux, L_Index, L_K, L_Max, or_1_out, or_2_out, print_dec_1_end, ReStart, RST_Max,
       S_Index, S_MO;
  wire [1:0] S_DM;
  wire [31:0] Max;

  or or_1 (or_1_out, demultiplexer_1_out0, ReStart);
  D_Flip_Flop d_ff_1 (.clk(CLK), .D(or_1_out), .Q(d_ff_1_q), .preset(Start));  // open: Qn, en, reset
  Demultiplexer #(.enable("false")) demultiplexer_1 (
    .out0(demultiplexer_1_out0), .out1(demultiplexer_1_out1), .in(d_ff_1_q), .sel(Start));
  Control_Unit control_unit_1 (
    .CLK(CLK), .Start(demultiplexer_1_out1), .Index___1(Index___2), .A__Index_____0(A__Index_____0),
    .A__Index_____Max___A__Index_____K(A__Index_____Max___A__Index_____K), .Index____2(Index____2),
    .End(End_CU), .S_MO(S_MO), .S_DM(S_DM), .Write(Write), .L_A__Index(L_A__Index),
    .L_A_____Index___1_____2(L_A____Index___1_____2), .S_Index(S_Index), .L_Index(L_Index), .L_Max(L_Max),
    .L_K(L_K), .RST_Max(RST_Max), .L_Aux(L_Aux));
  PRINT_DEC print_dec_1 (
    .num(Max), .start(End_CU), .CLK(CLK), .RST(Start), .ASCII(ASCII), .Write_ASCII(W_ASCII),
    .END(print_dec_1_end));
  or or_2 (or_2_out, print_dec_1_end, demultiplexer_2_out0);
  Demultiplexer #(.enable("false")) demultiplexer_2 (
    .out0(demultiplexer_2_out0), .out1(ReStart), .in(END), .sel(Start));
  D_Flip_Flop d_ff_2 (.clk(CLK), .D(or_2_out), .Q(END));  // open: Qn, preset, en, reset
  Data_Path data_path_1 (
    .CLK(CLK), .S_Index(S_Index), .S_Dir_Memory(S_DM), .RST_Max(RST_Max), .S_Memory_Out(S_MO),
    .Memory_Input(Memory_Input), .Data_Input(Data_Input), .L_Index(L_Index), .L_A__Index(L_A__Index),
    .L_Max(L_Max), .L_A_____Index___1_____2___1(L_A____Index___1_____2),
    .A__Index_____Max___A__Index_____K(A__Index_____Max___A__Index_____K), .Index___2(Index___2),
    .Index____1(Index____2), .A__Index_____0(A__Index_____0), .Dir_Memory(DM), .Memory_Out(MO), .Max(Max),
    .L_K(L_K), .L_Aux(L_Aux));

  // Other names for the same wires on the sheet: DI[31:0] = Data_Input; MI[31:0] = Memory_Input
endmodule
