// Logisim project BigASM Height.circ as structural Verilog
module BOARD_BIG_ASM (
  output out_1
);

  wire button_1_out, CLK, CLR, d_ff_1_q, not_1_out, Write, Write_ASCII;
  wire [6:0] ASCII;
  wire [7:0] counter_1_q;
  wire [23:0] Dir_INPUT, Dir_MEMORY;
  wire [31:0] INPUT, MEMORY_IN, MEMORY_OUT;

  Button button_1 (.out(button_1_out));
  Clock clock_1 (.out(CLK));
  D_Flip_Flop d_ff_1 (.clk(CLK), .D(1'b1), .Q(d_ff_1_q), .reset(button_1_out));  // open: Qn, preset, en
  D_Flip_Flop d_ff_2 (.clk(CLK), .D(d_ff_1_q), .Qn(CLR), .reset(button_1_out));  // open: Q, preset, en
  BIG_ASM big_asm_1 (
    .DATA_INPUT(INPUT), .MEMORY_IN(MEMORY_OUT), .CLK(CLK), .CLR(CLR), .DIR_INPUT(Dir_INPUT),
    .MEMORY_OUT(MEMORY_IN), .DIR_MEMORY(Dir_MEMORY), .Write_OUTPUT(Write), .ASCII(ASCII),
    .Write_ASCII(Write_ASCII), .END(out_1));
  MEMORY memory_1 (.DIR(Dir_MEMORY), .DATA_IN(MEMORY_IN), .WRITE(Write), .CLK(CLK), .CLR(CLR), .DATA_OUT(MEMORY_OUT));
  INPUT input_1 (.DIR(Dir_INPUT), .CLK(CLK), .DATA_OUT(INPUT));
  Counter counter_1 (.load(1'b0), .count(not_1_out), .Q(counter_1_q), .clk(CLK), .clr(CLR));  // open: D, carry
  not not_1 (not_1_out, out_1);
  // Probe on counter_1_q
  TTY #(.rows(32), .cols(60)) tty_1 (.data(ASCII), .clk(CLK), .we(Write_ASCII), .clr(CLR));

  // Other names for the same wires on the sheet: END = out_1

  // Notes on the sheet:
  //   COUNTER
  //   BOARD
endmodule

module INPUT (
  input  [23:0] DIR,
  input  CLK,
  output [31:0] DATA_OUT
);

  RAM #(.addrWidth(24), .dataWidth(32)) ram_1 (.addr(DIR), .data(DATA_OUT), .clk(CLK), .ld(1'b1));  // open: sel, clr
endmodule

module MEMORY (
  input  [23:0] DIR,
  input  [31:0] DATA_IN,
  input  WRITE,
  input  CLK,
  input  CLR,
  output [31:0] DATA_OUT
);

  RAM #(.addrWidth(24), .dataWidth(32), .bus("separate")) ram_1 (
    .addr(DIR), .din(DATA_IN), .data(DATA_OUT), .str(WRITE), .clk(CLK), .clr(CLR));  // open: sel, ld
endmodule

module BIG_ASM (
  input  [31:0] DATA_INPUT,
  input  [31:0] MEMORY_IN,
  input  CLK,
  input  CLR,
  output [23:0] DIR_INPUT,
  output [6:0] ASCII,
  output Write_ASCII,
  output [31:0] MEMORY_OUT,
  output END,
  output [23:0] DIR_MEMORY,
  output Write_OUTPUT
);

  Height height_1 (
    .Start(CLR), .CLK(CLK), .Data_Input(DATA_INPUT), .ASCII(ASCII), .W_ASCII(Write_ASCII), .END(END),
    .Dir_Input(DIR_INPUT));

  // Other names for the same wires on the sheet: DI[31:0] = DATA_INPUT
endmodule

module PRINT_UDEC (
  input  [31:0] num,
  input  start,
  input  CLK,
  input  RST,
  output [6:0] ASCII,
  output Write_ASCII,
  output \end 
);

  wire _0_c, _0_n, demultiplexer_1_out0, demultiplexer_2_out0, demultiplexer_2_out1, demultiplexer_3_out0,
       demultiplexer_3_out1, IDLE_2_q, IDLE_3_q, IDLE_4_q, IDLE_q, Lc, Lc_0, Ln, Ln_0, or_1_out;
  wire [23:0] bit_extender_1_out;
  wire [31:0] c, c___1, c___1_t, divider_1_rem, memory_1_data_out, multiplexer_1_out, multiplexer_2_out,
       multiplexer_3_out, n, n___10, n___10___48;

  Multiplexer #(.width(32), .enable("false")) multiplexer_1 (
    .in0(num), .in1(n___10), .out(multiplexer_1_out), .sel(Lc_0));
  Divider #(.width(32)) divider_1 (.a(n), .b(32'ha), .out(n___10), .rem(divider_1_rem));  // open: upper
  Adder #(.width(32)) adder_1 (.a(divider_1_rem), .b(32'h30), .out(n___10___48));  // open: cin, cout
  or or_1 (or_1_out, demultiplexer_1_out0, \end );
  Register #(.width(32)) u_n (.D(multiplexer_1_out), .en(Ln), .Q(n), .clk(CLK), .clr(RST));
  D_Flip_Flop IDLE (.clk(CLK), .D(or_1_out), .Q(IDLE_q), .preset(RST));  // open: Qn, en, reset
  Demultiplexer #(.enable("false")) demultiplexer_1 (
    .out0(demultiplexer_1_out0), .out1(Ln_0), .in(IDLE_q), .sel(start));
  or or_2 (Write_ASCII, demultiplexer_3_out0, demultiplexer_2_out1);
  Multiplexer #(.width(32), .enable("false")) multiplexer_2 (
    .in0(c___1), .in1(c___1_t), .out(multiplexer_2_out), .sel(Write_ASCII));
  Adder #(.width(32)) adder_2 (.a(c), .b(32'h1), .out(c___1));  // open: cin, cout
  Subtractor #(.width(32)) subtractor_1 (.a(c), .b(32'h1), .out(c___1_t));  // open: bin, bout
  D_Flip_Flop IDLE_2 (.clk(CLK), .D(Ln_0), .Q(IDLE_2_q), .reset(RST));  // open: Qn, preset, en
  Register #(.width(32)) u_c (.D(multiplexer_2_out), .en(Lc), .Q(c), .clk(CLK), .clr(RST));
  or or_3 (Lc_0, IDLE_2_q, demultiplexer_3_out1);
  Multiplexer #(.width(32), .enable("false")) multiplexer_3 (
    .in0(c), .in1(c___1_t), .out(multiplexer_3_out), .sel(Write_ASCII));
  Comparator #(.width(32), .mode("unsigned")) comparator_1 (.a({32{1'b0}}), .b(n), .lt(_0_n));  // open: gt, eq
  Comparator #(.width(32), .mode("unsigned")) comparator_2 (.a({32{1'b0}}), .b(c), .lt(_0_c));  // open: gt, eq
  D_Flip_Flop IDLE_3 (.clk(CLK), .D(Write_ASCII), .Q(IDLE_3_q), .reset(RST));  // open: Qn, preset, en
  Demultiplexer #(.enable("false")) demultiplexer_2 (
    .out0(demultiplexer_2_out0), .out1(demultiplexer_2_out1), .in(IDLE_3_q), .sel(_0_c));
  Bit_Extender #(.in_width(32), .out_width(24)) bit_extender_1 (.in(multiplexer_3_out), .out(bit_extender_1_out));
  D_Flip_Flop IDLE_4 (.clk(CLK), .D(Lc_0), .Q(IDLE_4_q), .reset(RST));  // open: Qn, preset, en
  or or_4 (Lc, Lc_0, Write_ASCII);
  or or_5 (Ln, Ln_0, Lc_0);
  Demultiplexer #(.enable("false")) demultiplexer_3 (
    .out0(demultiplexer_3_out0), .out1(demultiplexer_3_out1), .in(IDLE_4_q), .sel(_0_n));
  D_Flip_Flop IDLE_5 (.clk(CLK), .D(demultiplexer_2_out0), .Q(\end ), .reset(RST));  // open: Qn, preset, en
  MEMORY memory_1 (
    .DIR(bit_extender_1_out), .DATA_IN(n___10___48), .WRITE(Lc_0), .CLK(CLK), .CLR(RST),
    .DATA_OUT(memory_1_data_out));
  Bit_Extender #(.in_width(32), .out_width(7)) bit_extender_2 (.in(memory_1_data_out), .out(ASCII));

  // Other names for the same wires on the sheet: Lc_1 = Write_ASCII; Sc = Write_ASCII; Ln_1 = Lc_0; Sn = Lc_0;
  //   Write = Lc_0
endmodule

module PRINT_DEC (
  input  [31:0] num,
  input  start,
  input  CLK,
  input  RST,
  output [6:0] ASCII,
  output Write_ASCII,
  output END
);

  wire demultiplexer_1_out0, demultiplexer_1_out1, demultiplexer_2_out0, demultiplexer_3_out0, end_t,
       IDLE_3_q, IDLE_q, or_1_out, or_2_out, or_3_out, S_ASCII, startUDEC, Write_ASCII_1;
  wire [6:0] ASCII_t;
  wire [31:0] multiplexer_1_out, negator_1_out;

  or or_1 (or_1_out, demultiplexer_1_out0, END);
  Negator #(.width(32)) negator_1 (.in(num), .out(negator_1_out));
  D_Flip_Flop IDLE (.clk(CLK), .D(or_1_out), .Q(IDLE_q), .preset(RST));  // open: Qn, en, reset
  Demultiplexer #(.enable("false")) demultiplexer_1 (
    .out0(demultiplexer_1_out0), .out1(demultiplexer_1_out1), .in(IDLE_q), .sel(start));
  Multiplexer #(.width(32), .enable("false")) multiplexer_1 (
    .in0(num), .in1(negator_1_out), .out(multiplexer_1_out), .sel(num[31]));
  Demultiplexer #(.enable("false")) demultiplexer_2 (
    .out0(demultiplexer_2_out0), .out1(S_ASCII), .in(demultiplexer_1_out1), .sel(num[31]));
  or or_2 (or_2_out, demultiplexer_2_out0, S_ASCII);
  D_Flip_Flop IDLE_2 (.clk(CLK), .D(or_2_out), .Q(startUDEC), .reset(RST));  // open: Qn, preset, en
  PRINT_UDEC print_udec_1 (
    .num(multiplexer_1_out), .start(startUDEC), .CLK(CLK), .RST(RST), .ASCII(ASCII_t),
    .Write_ASCII(Write_ASCII_1), .\end (end_t));
  D_Flip_Flop IDLE_3 (.clk(CLK), .D(or_3_out), .Q(IDLE_3_q), .reset(RST));  // open: Qn, preset, en
  or or_3 (or_3_out, startUDEC, demultiplexer_3_out0);
  Demultiplexer #(.enable("false")) demultiplexer_3 (
    .out0(demultiplexer_3_out0), .out1(END), .in(IDLE_3_q), .sel(end_t));
  Multiplexer #(.width(7), .enable("false")) multiplexer_2 (
    .in0(ASCII_t), .in1(7'b0101101), .out(ASCII), .sel(S_ASCII));
  or or_4 (Write_ASCII, S_ASCII, Write_ASCII_1);

  // Other names for the same wires on the sheet: sign = num[31]; Write_ASCII_0 = S_ASCII
endmodule

module TEST_PRINT (
  input  [31:0] in_1,
  output out_2
);

  wire button_1_out, button_2_out, CLK, CLR, d_ff_1_q, Write_ASCII;
  wire [6:0] ASCII;

  Button button_1 (.out(button_1_out));
  Clock clock_1 (.out(CLK));
  D_Flip_Flop d_ff_1 (.clk(CLK), .D(1'b1), .Q(d_ff_1_q), .reset(button_1_out));  // open: Qn, preset, en
  D_Flip_Flop d_ff_2 (.clk(CLK), .D(d_ff_1_q), .Qn(CLR), .reset(button_1_out));  // open: Q, preset, en
  Button button_2 (.out(button_2_out));
  PRINT_UDEC print_udec_1 ();  // open: num, start, CLK, RST, ASCII, Write_ASCII, end
  PRINT_DEC print_dec_1 (
    .num(in_1), .start(button_2_out), .CLK(CLK), .RST(CLR), .ASCII(ASCII), .Write_ASCII(Write_ASCII),
    .END(out_2));
  TTY #(.rows(32), .cols(60)) tty_1 (.data(ASCII), .clk(CLK), .we(Write_ASCII), .clr(CLR));
endmodule

module Data_Path (
  input  CLK,
  input  [31:0] Data_Input,
  input  RST_Index,
  input  S_Height,
  input  S_j,
  input  L_j,
  input  L_Index,
  input  L_A_Index,
  input  L_lenght,
  input  L_LeafIndex,
  input  L_Height,
  output out_12,
  output out_13,
  output out_14,
  output [31:0] out_15,
  output [23:0] out_16
);

  wire comparator_1_eq, comparator_1_lt, comparator_2_eq, comparator_2_gt;
  wire [23:0] Index___1, Index_plus_plus, LeafIndex;
  wire [31:0] A___Index, adder_3_out, bit_extender_1_out, bit_extender_2_out, divider_1_out, h_plus_plus, j,
       j___1_____2___1, lenght, multiplexer_1_out, multiplexer_2_out;

  Register #(.width(24)) Index (.D(Index_plus_plus), .en(L_Index), .Q(out_16), .clk(CLK), .clr(RST_Index));
  Register #(.width(32)) A__Index (.D(Data_Input), .en(L_A_Index), .Q(A___Index), .clk(CLK));  // open: clr
  assign bit_extender_1_out = {{8{1'b0}}, LeafIndex};  // Bit_Extender bit_extender_1
  Subtractor #(.width(24)) subtractor_1 (.a(out_16), .b(24'h1), .out(Index___1));  // open: bin, bout
  Adder #(.width(24)) adder_1 (.a(out_16), .b(24'h1), .out(Index_plus_plus));  // open: cin, cout
  Adder #(.width(32)) adder_2 (.a(out_15), .b(32'h1), .out(h_plus_plus));  // open: cin, cout
  Adder #(.width(32)) adder_3 (.a(j), .b(32'h1), .out(adder_3_out));  // open: cin, cout
  Multiplexer #(.width(32), .enable("false")) multiplexer_1 (
    .in0(bit_extender_1_out), .in1(j___1_____2___1), .out(multiplexer_1_out), .sel(S_j));
  Register #(.width(32)) u_j (.D(multiplexer_1_out), .en(L_j), .Q(j), .clk(CLK));  // open: clr
  Divider #(.width(32)) divider_1 (.a(adder_3_out), .b(32'h2), .out(divider_1_out));  // open: upper, rem
  Register #(.width(32)) u_lenght (.D(Data_Input), .en(L_lenght), .Q(lenght), .clk(CLK));  // open: clr
  Subtractor #(.width(32)) subtractor_2 (.a(divider_1_out), .b(32'h1), .out(j___1_____2___1));  // open: bin, bout
  assign bit_extender_2_out = {{8{1'b0}}, out_16};  // Bit_Extender bit_extender_2
  Comparator #(.width(32)) comparator_1 (
    .a(bit_extender_2_out), .b(lenght), .eq(comparator_1_eq), .lt(comparator_1_lt));  // open: gt
  Comparator #(.width(32)) comparator_2 (
    .a(j___1_____2___1), .b({32{1'b0}}), .gt(comparator_2_gt), .eq(comparator_2_eq));  // open: lt
  Comparator #(.width(32)) comparator_3 (.a(A___Index), .b({32{1'b0}}), .gt(out_14));  // open: eq, lt
  Register #(.width(24)) u_LeafIndex (.D(Index___1), .en(L_LeafIndex), .Q(LeafIndex), .clk(CLK));  // open: clr
  or or_1 (out_12, comparator_1_eq, comparator_1_lt);
  or or_2 (out_13, comparator_2_gt, comparator_2_eq);
  Multiplexer #(.width(32), .enable("false")) multiplexer_2 (
    .in0(32'h1), .in1(h_plus_plus), .out(multiplexer_2_out), .sel(S_Height));
  Register #(.width(32)) Height (.D(multiplexer_2_out), .en(L_Height), .Q(out_15), .clk(CLK));  // open: clr

  // Other names for the same wires on the sheet: A___Index_____0 = out_14; DI[31:0] = Data_Input; h[31:0] = out_15;
  //   Index[23:0] = out_16; Index____lenght = out_12; j___1_____2___1____0 = out_13
endmodule

module Control_Unit (
  input  Start,
  input  CLK,
  input  Index____lenght,
  input  j___1_____2___1____0,
  input  A___Index_____0,
  output RST_Index,
  output L_Height,
  output S__Height,
  output L_lenght,
  output L_index,
  output L_j,
  output S_j,
  output L_LeafIndex,
  output End,
  output L_A__Index
);

  wire d_ff_2_q, demultiplexer_1_out0, demultiplexer_2_out1, demultiplexer_5_out0, demultiplexer_5_out1,
       End_q, IDLE_q, L_index2, L_j0, or_1_out, or_4_out, or_6_out, or_7_out, While1_q, While2_q;

  D_Flip_Flop IDLE (.clk(CLK), .D(or_1_out), .Q(IDLE_q), .preset(Start));  // open: Qn, en, reset
  or or_1 (or_1_out, demultiplexer_1_out0, demultiplexer_5_out1);
  or or_2 (L_index, L_lenght, L_LeafIndex, L_index2);
  Demultiplexer #(.enable("false")) demultiplexer_1 (
    .out0(demultiplexer_1_out0), .out1(L_lenght), .in(IDLE_q), .sel(Start));
  or or_3 (L_Height, L_lenght, S__Height);
  or or_4 (or_4_out, L_lenght, L_index2, L_LeafIndex);
  D_Flip_Flop While1 (.clk(CLK), .D(or_4_out), .Q(While1_q));  // open: Qn, preset, en, reset
  Demultiplexer #(.enable("false")) demultiplexer_2 (
    .out0(L_j0), .out1(demultiplexer_2_out1), .in(While1_q), .sel(Index____lenght));
  or or_5 (L_j, L_j0, S__Height);
  D_Flip_Flop d_ff_1 (.clk(CLK), .D(demultiplexer_2_out1), .Q(L_A__Index));  // open: Qn, preset, en, reset
  D_Flip_Flop d_ff_2 (.clk(CLK), .D(L_A__Index), .Q(d_ff_2_q));  // open: Qn, preset, en, reset
  Demultiplexer #(.enable("false")) demultiplexer_3 (
    .out0(L_index2), .out1(L_LeafIndex), .in(d_ff_2_q), .sel(A___Index_____0));
  or or_6 (or_6_out, L_j0, S__Height);
  Demultiplexer #(.enable("false")) demultiplexer_4 (
    .out0(End), .out1(S__Height), .in(While2_q), .sel(j___1_____2___1____0));
  D_Flip_Flop While2 (.clk(CLK), .D(or_6_out), .Q(While2_q));  // open: Qn, preset, en, reset
  Demultiplexer #(.enable("false")) demultiplexer_5 (
    .out0(demultiplexer_5_out0), .out1(demultiplexer_5_out1), .in(End_q), .sel(Start));
  D_Flip_Flop u_End (.clk(CLK), .D(or_7_out), .Q(End_q));  // open: Qn, preset, en, reset
  or or_7 (or_7_out, End, demultiplexer_5_out0);

  assign RST_Index = Start;
  assign S_j = S__Height;

  // Other names for the same wires on the sheet: L_Height0 = L_lenght; L_index0 = L_lenght; L_index1 = L_LeafIndex;
  //   L_Height1 = S__Height; L_j1 = S__Height
endmodule

module Height (
  input  Start,
  input  CLK,
  input  [31:0] Data_Input,
  output [23:0] Dir_Input,
  output [6:0] ASCII,
  output W_ASCII,
  output END
);

  wire control_unit_1_l_a__index, control_unit_1_l_height, control_unit_1_l_index, control_unit_1_l_j,
       control_unit_1_l_leafindex, control_unit_1_l_lenght, control_unit_1_rst_index,
       control_unit_1_s__height, control_unit_1_s_j, d_ff_1_q, data_path_1_out_12, data_path_1_out_13,
       data_path_1_out_14, demultiplexer_1_out0, demultiplexer_1_out1, demultiplexer_2_out0, End_t, or_1_out,
       or_2_out, print_udec_1_end, ReStart;
  wire [31:0] Height;

  D_Flip_Flop d_ff_1 (.clk(CLK), .D(or_1_out), .Q(d_ff_1_q), .preset(Start));  // open: Qn, en, reset
  or or_1 (or_1_out, demultiplexer_1_out0, ReStart);
  Demultiplexer #(.enable("false")) demultiplexer_1 (
    .out0(demultiplexer_1_out0), .out1(demultiplexer_1_out1), .in(d_ff_1_q), .sel(Start));
  PRINT_UDEC print_udec_1 (
    .num(Height), .start(End_t), .CLK(CLK), .RST(Start), .ASCII(ASCII), .Write_ASCII(W_ASCII),
    .\end (print_udec_1_end));
  Control_Unit control_unit_1 (
    .Start(demultiplexer_1_out1), .CLK(CLK), .Index____lenght(data_path_1_out_12),
    .j___1_____2___1____0(data_path_1_out_13), .A___Index_____0(data_path_1_out_14),
    .RST_Index(control_unit_1_rst_index), .L_Height(control_unit_1_l_height),
    .S__Height(control_unit_1_s__height), .L_lenght(control_unit_1_l_lenght),
    .L_index(control_unit_1_l_index), .L_j(control_unit_1_l_j), .S_j(control_unit_1_s_j),
    .L_LeafIndex(control_unit_1_l_leafindex), .End(End_t), .L_A__Index(control_unit_1_l_a__index));
  or or_2 (or_2_out, print_udec_1_end, demultiplexer_2_out0);
  D_Flip_Flop d_ff_2 (.clk(CLK), .D(or_2_out), .Q(END));  // open: Qn, preset, en, reset
  Demultiplexer #(.enable("false")) demultiplexer_2 (
    .out0(demultiplexer_2_out0), .out1(ReStart), .in(END), .sel(Start));
  Data_Path data_path_1 (
    .CLK(CLK), .Data_Input(Data_Input), .RST_Index(control_unit_1_rst_index),
    .S_Height(control_unit_1_s__height), .S_j(control_unit_1_s_j), .L_j(control_unit_1_l_j),
    .L_Index(control_unit_1_l_index), .L_A_Index(control_unit_1_l_a__index),
    .L_lenght(control_unit_1_l_lenght), .L_LeafIndex(control_unit_1_l_leafindex),
    .L_Height(control_unit_1_l_height), .out_12(data_path_1_out_12), .out_13(data_path_1_out_13),
    .out_14(data_path_1_out_14), .out_15(Height), .out_16(Dir_Input));

  // Other names for the same wires on the sheet: DI[31:0] = Data_Input
endmodule
